# Fritzing sketch main (saved by Fritzing 0.9.2b)
breadboards: 1

parts:
  Raspberry_Pi1 = Raspberry Pi 2
  Part1 = Barometric Pressure Sensor - BMP085 Breakout
  Raspberry_Pi_Zero1 = Raspberry Pi Zero
  Part2 = Barometric Pressure Sensor - BMP085 Breakout

nets:
  3V3: Raspberry_Pi1.3V3, Part1.Vcc, Raspberry_Pi_Zero1.3v3, Part2.Vcc
  GND: Raspberry_Pi1.GND, Part1.GND, Raspberry_Pi_Zero1.GND, Part2.GND
  N1: Raspberry_Pi1.GPIO15, Part1.RXD
  N2: Raspberry_Pi1.GPIO14, Part1.TXD
  N3: Raspberry_Pi_Zero1.GIPO15, Part2.RXD
  N4: Raspberry_Pi_Zero1.GIPO14, Part2.TXD

custom parts:
  Barometric Pressure Sensor - BMP085 Breakout: Description: This is a simple breakout board for the BMP085 high-precision, low-power barometric pressure sensor. The BMP085 offers a measuring range of 300 to 1100 hPa with an absolute accuracy of down to 0.03 hPa. It's based on piezo-resistive technology for EMC robustness, high accuracy and linearity as well as long term stability. This sensor supports a voltage supply between 1.8 and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
