# Fritzing sketch mm_roaming (saved by Fritzing 0.9.2b)

parts:
  Raspberry_Pi_Zero1 = Raspberry Pi Zero
  GY-NEO6MV3 = SUP500F [package=sup500f]
  U1 = LIPO-2000mAh [package=lipo-2000]
  InAir4 = InAir4
  PiScreen = PiScreen_1 [package=2x10_lock]
  U2 = PiScreen_2 [package=2x10_lock]
  Part1 = Power Cell LiPo Charger/Booster
  U3 = LIPO-2000mAh [package=lipo-2000]
  S1 = Toggle Switch [package=THT]

nets:
  3V3: Raspberry_Pi_Zero1.3v3, Raspberry_Pi_Zero1.3V3, GY-NEO6MV3.TX-O, InAir4.3V3, PiScreen.1_(3.3V)
  N1: Raspberry_Pi_Zero1.GIPO4, InAir4.VS
  GND: Raspberry_Pi_Zero1.GND, GY-NEO6MV3.RX-I, U1.-, InAir4.0V, Part1.GND, U3.-
  N2: Raspberry_Pi_Zero1.GIPO17, PiScreen.11_(TP_INT)
  N3: Raspberry_Pi_Zero1.GIPO22, PiScreen.15_(BACKLIGHT)
  N4: Raspberry_Pi_Zero1.GIPO10, InAir4.SI, PiScreen.19_(LCD_SI_/_TP_SI)
  N5: Raspberry_Pi_Zero1.GIPO9, InAir4.SO, U2.21_(TP_SO)
  N6: Raspberry_Pi_Zero1.GIPO11, InAir4.CK
  N7: Raspberry_Pi_Zero1.GIPO5, InAir4.D2
  N8: Raspberry_Pi_Zero1.GIPO6, InAir4.D3
  N9: Raspberry_Pi_Zero1.GIPO13, InAir4.D0
  N10: Raspberry_Pi_Zero1.GIPO20, InAir4.CS
  N11: Raspberry_Pi_Zero1.GIPO7, U2.26_(TP_CS)
  N12: Raspberry_Pi_Zero1.GIPO8, U2.24_(LCD_CS)
  N13: Raspberry_Pi_Zero1.GIPO25, U2.22_(RST)
  N14: Raspberry_Pi_Zero1.GIPO24, PiScreen.18_(LCD_RS)
  N15: Raspberry_Pi_Zero1.GIPO23, InAir4.D1
  N16: Raspberry_Pi_Zero1.GIPO15, GY-NEO6MV3.VCC
  N17: Raspberry_Pi_Zero1.GIPO14, GY-NEO6MV3.GND
  N18: Raspberry_Pi_Zero1.5V, PiScreen.2_(5V), S1.COM
  N19: U1.+, Part1.VCC, U3.+
  N20: Part1.5VIN, S1.L2

notes:
  GND: Grey / Black
  VCC: Red/Orange/Grey (3.3v)
  RX: Blue
  TX: Green
  LiPo Red --> B+
  LiPo Black --> B-
  - 60cm lengths
  - Strip wires to pad length (both sides first)
  - tin wires
  Soldering Iron: ~250c
  Wire: 24gauge Stranded

custom parts:
  PiScreen_1: This was SPECIALLY designed to be used with our Graphic LCD Backpack. Be sure you want to use this! It is not only staggered on each line of header holes, but IT IS ALSO offset of the center point of the top and bottom lines by 5 mil. This causes the headers to lock into place on the standard footprint on the LCD screen. The extra squares on the tdocu layer are there simply to reference other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
  PiScreen_2: This was SPECIALLY designed to be used with our Graphic LCD Backpack. Be sure you want to use this! It is not only staggered on each line of header holes, but IT IS ALSO offset of the center point of the top and bottom lines by 5 mil. This causes the headers to lock into place on the standard footprint on the LCD screen. The extra squares on the tdocu layer are there simply to reference other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
